// Logisim project homework_1.circ as structural Verilog
module main (
);

  wire [3:0] undriven, undriven_2, undriven_3, undriven_4;

  ROM rom_1 ();  // open: addr, data, sel
  Hex_Digit_Display hex_digit_display_1 (.value(undriven_4));  // open: dp
  Hex_Digit_Display hex_digit_display_2 (.value(undriven_3));  // open: dp
  Hex_Digit_Display hex_digit_display_3 (.value(undriven_2));  // open: dp
  Hex_Digit_Display hex_digit_display_4 (.value(undriven));  // open: dp
endmodule

module circuit_bank (
  input  ZF,
  input  [2:0] HEX_VALUE,
  output IRLD,
  output MEMLD,
  output MUX,
  output ZFLD,
  output REGLD,
  output ARMUX,
  output LOAD,
  output PCINC,
  output PCLD
);

  wire [1:1] and_1_out;
  wire [2:0] multiplexer_1_out, multiplexer_2_out, register_1_q, undriven;
  wire [8:8] rom_1_data;

  Register #(.width(3)) register_1 (.D(multiplexer_1_out), .Q(register_1_q), .clk(LOAD));  // open: en, clr
  and and_1 (and_1_out[1], ~undriven[0], ~undriven[1], undriven[2]);  // AND_Gate
  Multiplexer #(.width(3)) multiplexer_1 (
    .in0(3'b000), .in1(multiplexer_2_out), .out(multiplexer_1_out), .sel(rom_1_data[8]));  // open: en
  Multiplexer #(.select(2), .width(3)) multiplexer_2 (
    .in0(HEX_VALUE), .in1(undriven), .in2(3'b000), .in3(3'b101), .out(multiplexer_2_out),
    .sel({and_1_out[1], ZF}));  // open: en
  ROM #(.addrWidth(3), .dataWidth(9)) rom_1 (
    .addr(register_1_q), .data({rom_1_data[8], PCLD, PCINC, ARMUX, REGLD, ZFLD, MUX, MEMLD, IRLD}));  // open: sel

  // Notes on the sheet:
  //   contents of rom_1 (hex, n*v repeats v):
  //   141 54 34 22 0 80 0 18
endmodule

module register_bank (
  input  REG_LD,
  input  CLK
);

  _16_bit_register u_16_bit_register_1 ();  // open: DATA_IN, CLK, LOAD, DATA_OUT
endmodule

module register (
  input  DATA_IN,
  input  CLK,
  input  LOAD,
  output DATA__OUT
);

  wire not_1_out;

  not not_1 (not_1_out, DATA_IN);
  S_R_Flip_Flop s_r_ff_1 (.S(DATA_IN), .clk(CLK), .R(not_1_out), .Q(DATA__OUT), .en(LOAD));  // open: Qn, preset, reset
endmodule

module _16_bit_register (
  input  [15:0] DATA_IN,
  input  CLK,
  input  LOAD,
  output [15:0] DATA_OUT
);

  register register_1 (.DATA_IN(DATA_IN[0]), .CLK(CLK), .LOAD(LOAD), .DATA__OUT(DATA_OUT[0]));
  register register_2 (.DATA_IN(DATA_IN[1]), .CLK(CLK), .LOAD(LOAD), .DATA__OUT(DATA_OUT[1]));
  register register_3 (.DATA_IN(DATA_IN[2]), .CLK(CLK), .LOAD(LOAD), .DATA__OUT(DATA_OUT[2]));
  register register_4 (.DATA_IN(DATA_IN[3]), .CLK(CLK), .LOAD(LOAD), .DATA__OUT(DATA_OUT[3]));
  register register_5 (.DATA_IN(DATA_IN[4]), .CLK(CLK), .LOAD(LOAD), .DATA__OUT(DATA_OUT[4]));
  register register_6 (.DATA_IN(DATA_IN[5]), .CLK(CLK), .LOAD(LOAD), .DATA__OUT(DATA_OUT[5]));
  register register_7 (.DATA_IN(DATA_IN[6]), .CLK(CLK), .LOAD(LOAD), .DATA__OUT(DATA_OUT[6]));
  register register_8 (.DATA_IN(DATA_IN[7]), .CLK(CLK), .LOAD(LOAD), .DATA__OUT(DATA_OUT[7]));
  register register_9 (.DATA_IN(DATA_IN[8]), .CLK(CLK), .LOAD(LOAD), .DATA__OUT(DATA_OUT[8]));
  register register_10 (.DATA_IN(DATA_IN[9]), .CLK(CLK), .LOAD(LOAD), .DATA__OUT(DATA_OUT[9]));
  register register_11 (.DATA_IN(DATA_IN[10]), .CLK(CLK), .LOAD(LOAD), .DATA__OUT(DATA_OUT[10]));
  register register_12 (.DATA_IN(DATA_IN[11]), .CLK(CLK), .LOAD(LOAD), .DATA__OUT(DATA_OUT[11]));
  register register_13 (.DATA_IN(DATA_IN[12]), .CLK(CLK), .LOAD(LOAD), .DATA__OUT(DATA_OUT[12]));
  register register_14 (.DATA_IN(DATA_IN[13]), .CLK(CLK), .LOAD(LOAD), .DATA__OUT(DATA_OUT[13]));
  register register_15 (.DATA_IN(DATA_IN[14]), .CLK(CLK), .LOAD(LOAD), .DATA__OUT(DATA_OUT[14]));
  register register_16 (.DATA_IN(DATA_IN[15]), .CLK(CLK), .LOAD(LOAD), .DATA__OUT(DATA_OUT[15]));
endmodule
