// Logisim project project_2.circ as structural Verilog: 2 circuits, main circuit main
module main (
  input  [15:0] Pin_1,
  input  [15:0] Pin_2
);

  wire _7_SEG_LD, ADDR_0, ADDR_1, CLK, CS, main_1_out_2, main_1_out_3, main_1_out_4, main_1_out_5,
       main_2_out_6, main_2_out_7, main_2_out_8, main_3_out_2, main_3_out_3, main_3_out_4, main_3_out_5,
       main_4_out_6, main_4_out_7, main_4_out_8, main_5_out_2, main_5_out_3, main_5_out_4, main_5_out_5,
       main_6_out_6, main_6_out_7, main_6_out_8, main_7_out_6, main_7_out_7, main_7_out_8, main_8_out_2,
       main_8_out_3, main_8_out_4, main_8_out_5, MEMLD, not_1_out, not_2_out, not_3_out, not_4_out,
       not_5_out, PB_1, PB_2;
  wire [3:0] DISP_0, DISP_1, DISP_2, DISP_3;
  wire [15:0] DATA_IN, DATA_OUT, IN_1_OUT, IN_2_OUT, multiplexer_1_out, multiplexer_2_out;
  wire [15:2] ADDR_OUT;

  Clock clock_1 (.out(CLK));
  _7_segment_driver_main main_1 (
    .in_1(DISP_0), .out_2(main_1_out_2), .out_3(main_1_out_3), .out_4(main_1_out_4), .out_5(main_1_out_5));  // open: out_6, out_7, out_8
  _7_Segment_Display u_7_segment_display_1 (
    .g(main_1_out_5), .f(main_1_out_4), .a(main_1_out_3), .b(main_1_out_2), .e(main_2_out_8),
    .d(main_2_out_7), .c(main_2_out_6));  // open: dp
  _7_segment_driver_main main_2 (
    .in_1(DISP_0), .out_6(main_2_out_6), .out_7(main_2_out_7), .out_8(main_2_out_8));  // open: out_2, out_3, out_4, out_5
  Button button_1 (.out(PB_1));
  Button button_2 (.out(PB_2));
  _7_segment_driver_main main_3 (
    .in_1(DISP_1), .out_2(main_3_out_2), .out_3(main_3_out_3), .out_4(main_3_out_4), .out_5(main_3_out_5));  // open: out_6, out_7, out_8
  _7_Segment_Display u_7_segment_display_2 (
    .g(main_3_out_5), .f(main_3_out_4), .a(main_3_out_3), .b(main_3_out_2), .e(main_4_out_8),
    .d(main_4_out_7), .c(main_4_out_6));  // open: dp
  _7_segment_driver_main main_4 (
    .in_1(DISP_1), .out_6(main_4_out_6), .out_7(main_4_out_7), .out_8(main_4_out_8));  // open: out_2, out_3, out_4, out_5
  _7_segment_driver_main main_5 (
    .in_1(DISP_2), .out_2(main_5_out_2), .out_3(main_5_out_3), .out_4(main_5_out_4), .out_5(main_5_out_5));  // open: out_6, out_7, out_8
  _7_Segment_Display u_7_segment_display_3 (
    .g(main_5_out_5), .f(main_5_out_4), .a(main_5_out_3), .b(main_5_out_2), .e(main_7_out_8),
    .d(main_7_out_7), .c(main_7_out_6));  // open: dp
  _7_segment_driver_main main_6 (
    .in_1(DISP_3), .out_6(main_6_out_6), .out_7(main_6_out_7), .out_8(main_6_out_8));  // open: out_2, out_3, out_4, out_5
  _7_segment_driver_main main_7 (
    .in_1(DISP_2), .out_6(main_7_out_6), .out_7(main_7_out_7), .out_8(main_7_out_8));  // open: out_2, out_3, out_4, out_5
  _7_segment_driver_main main_8 (
    .in_1(DISP_3), .out_2(main_8_out_2), .out_3(main_8_out_3), .out_4(main_8_out_4), .out_5(main_8_out_5));  // open: out_6, out_7, out_8
  _7_Segment_Display u_7_segment_display_4 (
    .g(main_8_out_5), .f(main_8_out_4), .a(main_8_out_3), .b(main_8_out_2), .e(main_6_out_8),
    .d(main_6_out_7), .c(main_6_out_6));  // open: dp
  input_selector input_selector_1 (.IN(Pin_1), .PB(PB_1), .CLK(CLK), .CS(CS), .OUT(IN_1_OUT), .ADDR_0(ADDR_0));
  input_selector input_selector_2 (.IN(Pin_2), .PB(PB_2), .CLK(CLK), .CS(CS), .OUT(IN_2_OUT), .ADDR_0(ADDR_0));
  _16_bit_register u_16_bit_register_1 (
    .IN(DATA_OUT), .LD(_7_SEG_LD), .CLK(CLK), .OUT({DISP_0, DISP_1, DISP_2, DISP_3}));
  Multiplexer #(.width(16), .enable("false")) multiplexer_1 (
    .in0(IN_1_OUT), .in1(IN_2_OUT), .out(multiplexer_1_out), .sel(ADDR_1));
  Multiplexer #(.width(16), .enable("false")) multiplexer_2 (
    .in0(DATA_IN), .in1(multiplexer_1_out), .out(multiplexer_2_out), .sel(CS));
  and and_1 (CS, ADDR_OUT[15], ADDR_OUT[14], ADDR_OUT[13], ADDR_OUT[12], ADDR_OUT[11], ADDR_OUT[10], ADDR_OUT[9], ADDR_OUT[8], ADDR_OUT[7], ADDR_OUT[6], ADDR_OUT[5], ADDR_OUT[4], not_1_out, not_2_out, 1'b1, 1'b1);
  not not_1 (not_1_out, ADDR_OUT[3]);
  not not_2 (not_2_out, ADDR_OUT[2]);
  RAM #(.addrWidth(16), .dataWidth(16), .bus("separate")) ram_1 (
    .addr({ADDR_OUT, ADDR_1, ADDR_0}), .din(DATA_OUT), .data(DATA_IN), .str(MEMLD), .clk(CLK));  // open: sel, ld, clr
  CPU cpu_1 (
    .DATA_IN(multiplexer_2_out), .CLK(CLK), .MEMLD(MEMLD), .ADDR_OUT({ADDR_OUT, ADDR_1, ADDR_0}),
    .DATA_OUT(DATA_OUT));
  and and_2 (_7_SEG_LD, ADDR_OUT[15], ADDR_OUT[14], ADDR_OUT[13], ADDR_OUT[12], ADDR_OUT[11], ADDR_OUT[10], ADDR_OUT[9], ADDR_OUT[8], ADDR_OUT[7], ADDR_OUT[6], ADDR_OUT[5], ADDR_OUT[4], not_4_out, ADDR_OUT[2], not_3_out, not_5_out);
  not not_3 (not_3_out, ADDR_1);
  not not_4 (not_4_out, ADDR_OUT[3]);
  not not_5 (not_5_out, ADDR_0);

  // Other names for the same wires on the sheet: ADDR_OUT[1:0] = {ADDR_1, ADDR_0}
endmodule

module input_selector (
  input  [15:0] IN,
  input  PB,
  input  CLK,
  input  CS,
  input  ADDR_0,
  output [15:0] OUT
);

  wire and_1_out, and_2_out, and_3_out, not_1_out;
  wire [0:0] s_r_ff_1_q;
  wire [15:0] n16_bit_register_1_out;

  not not_1 (not_1_out, s_r_ff_1_q[0]);
  and and_1 (and_1_out, CS, ADDR_0);
  and and_2 (and_2_out, not_1_out, PB);
  and and_3 (and_3_out, and_1_out, s_r_ff_1_q[0]);
  _16_bit_register u_16_bit_register_1 (.IN(IN), .LD(and_2_out), .CLK(CLK), .OUT(n16_bit_register_1_out));
  S_R_Flip_Flop s_r_ff_1 (.S(and_2_out), .clk(CLK), .R(and_3_out), .Q(s_r_ff_1_q[0]));  // open: Qn, preset, reset, en
  Multiplexer #(.width(16), .enable("false")) multiplexer_1 (
    .in0(n16_bit_register_1_out), .in1({{15{1'b0}}, s_r_ff_1_q[0]}), .out(OUT), .sel(ADDR_0));
endmodule
