// Logisim project project_3.circ as structural Verilog: 2 circuits, main circuit main
module main (
  input  [15:0] switch_2,
  input  [15:0] switch_1
);

  wire button_1_out, CLK, CPU_INT, CPU_INT_ACK, CS, main_1_out_2, main_1_out_3, main_1_out_4, main_1_out_5,
       main_2_out_6, main_2_out_7, main_2_out_8, main_3_out_2, main_3_out_3, main_3_out_4, main_3_out_5,
       main_4_out_6, main_4_out_7, main_4_out_8, main_5_out_2, main_5_out_3, main_5_out_4, main_5_out_5,
       main_6_out_6, main_6_out_7, main_6_out_8, main_7_out_2, main_7_out_3, main_7_out_4, main_7_out_5,
       main_8_out_6, main_8_out_7, main_8_out_8, main_9_out_2, main_9_out_3, main_9_out_4, main_9_out_5,
       main_10_out_6, main_10_out_7, main_10_out_8, main_11_out_2, main_11_out_3, main_11_out_4,
       main_11_out_5, main_12_out_6, main_12_out_7, main_12_out_8, main_13_out_2, main_13_out_3,
       main_13_out_4, main_13_out_5, main_14_out_6, main_14_out_7, main_14_out_8, main_15_out_2,
       main_15_out_3, main_15_out_4, main_15_out_5, main_16_out_6, main_16_out_7, main_16_out_8, MEMLD,
       OUT_EN, RES_LD, TIME_LD, timer_1_time_int;
  wire [2:0] priority_encoder_1_out;
  wire [15:0] ADDR, CPU_DIN, CPU_DOUT, INT_VECTOR, MEM_DOUT, multiplexer_1_out, multiplexer_2_out, PB_DAT,
       RES_OUT, TIME_DAT, TIME_OUT;

  Clock clock_1 (.out(CLK));
  Button button_1 (.out(button_1_out));
  assign PB_DAT = {{15{1'b0}}, button_1_out};  // Bit_Extender bit_extender_1
  and and_1 (CS, ADDR[15], ADDR[14], ADDR[13], ADDR[12], ADDR[11], ADDR[10], ADDR[9], ADDR[8], ADDR[7], ADDR[6], ADDR[5], ADDR[4], ADDR[3], ADDR[2], 1'b1, 1'b1);
  and and_2 (OUT_EN, ADDR[15], ADDR[14], ADDR[13], ADDR[12], ADDR[11], ADDR[10], ADDR[9], ADDR[8], ADDR[7], ADDR[6], ADDR[5], ADDR[4], ~ADDR[3], ~ADDR[2], ~ADDR[1], 1'b1);  // AND_Gate
  RAM #(.addrWidth(16), .dataWidth(16), .bus("separate")) ram_1 (
    .addr(ADDR), .din(CPU_DOUT), .data(MEM_DOUT), .str(MEMLD), .clk(CLK));  // open: sel, ld, clr
  timer timer_1 (.CLK(CLK), .TIME_INT(timer_1_time_int), .TIME(TIME_DAT));
  _16_bit_register u_16_bit_register_1 (.IN(CPU_DOUT), .LD(RES_LD), .CLK(CLK), .OUT(RES_OUT));
  Multiplexer #(.select(2), .width(16), .enable("false")) multiplexer_1 (
    .in0(switch_1), .in1(switch_2), .in2(PB_DAT), .in3(TIME_DAT), .out(multiplexer_1_out), .sel(ADDR[1:0]));
  Priority_Encoder priority_encoder_1 (
    .in0(timer_1_time_int), .out(priority_encoder_1_out), .en_in(1'b1), .gs(CPU_INT));  // open: in1, in2, in3, in4, in5, in6, in7, en_out
  Multiplexer #(.width(16), .enable("false")) multiplexer_2 (
    .in0(MEM_DOUT), .in1(multiplexer_1_out), .out(multiplexer_2_out), .sel(CS));
  assign INT_VECTOR = {{13{1'b0}}, priority_encoder_1_out};  // Bit_Extender bit_extender_2
  Decoder #(.disabled(0)) decoder_1 (.out0(TIME_LD), .out1(RES_LD), .sel(ADDR[0]), .en(OUT_EN));
  Vertebrate_CPU vertebrate_cpu_1 (
    .DATA_IN(CPU_DIN), .CLK(CLK), .INT(CPU_INT), .MEMLD(MEMLD), .INTACK(CPU_INT_ACK), .ADDR_OUT(ADDR),
    .DATA_OUT(CPU_DOUT));
  Multiplexer #(.width(16), .enable("false")) multiplexer_3 (
    .in0(multiplexer_2_out), .in1(INT_VECTOR), .out(CPU_DIN), .sel(CPU_INT_ACK));
  _7_segment_driver_main main_1 (
    .in_1(TIME_OUT[15:12]), .out_2(main_1_out_2), .out_3(main_1_out_3), .out_4(main_1_out_4),
    .out_5(main_1_out_5));  // open: out_6, out_7, out_8
  _7_Segment_Display u_7_segment_display_1 (
    .g(main_1_out_5), .f(main_1_out_4), .a(main_1_out_3), .b(main_1_out_2), .e(main_2_out_8),
    .d(main_2_out_7), .c(main_2_out_6));  // open: dp
  _7_segment_driver_main main_2 (
    .in_1(TIME_OUT[15:12]), .out_6(main_2_out_6), .out_7(main_2_out_7), .out_8(main_2_out_8));  // open: out_2, out_3, out_4, out_5
  _7_segment_driver_main main_3 (
    .in_1(RES_OUT[15:12]), .out_2(main_3_out_2), .out_3(main_3_out_3), .out_4(main_3_out_4),
    .out_5(main_3_out_5));  // open: out_6, out_7, out_8
  _7_Segment_Display u_7_segment_display_2 (
    .g(main_3_out_5), .f(main_3_out_4), .a(main_3_out_3), .b(main_3_out_2), .e(main_4_out_8),
    .d(main_4_out_7), .c(main_4_out_6));  // open: dp
  _7_segment_driver_main main_4 (
    .in_1(RES_OUT[15:12]), .out_6(main_4_out_6), .out_7(main_4_out_7), .out_8(main_4_out_8));  // open: out_2, out_3, out_4, out_5
  _7_segment_driver_main main_5 (
    .in_1(TIME_OUT[11:8]), .out_2(main_5_out_2), .out_3(main_5_out_3), .out_4(main_5_out_4),
    .out_5(main_5_out_5));  // open: out_6, out_7, out_8
  _7_Segment_Display u_7_segment_display_3 (
    .g(main_5_out_5), .f(main_5_out_4), .a(main_5_out_3), .b(main_5_out_2), .e(main_6_out_8),
    .d(main_6_out_7), .c(main_6_out_6));  // open: dp
  _7_segment_driver_main main_6 (
    .in_1(TIME_OUT[11:8]), .out_6(main_6_out_6), .out_7(main_6_out_7), .out_8(main_6_out_8));  // open: out_2, out_3, out_4, out_5
  _7_segment_driver_main main_7 (
    .in_1(RES_OUT[11:8]), .out_2(main_7_out_2), .out_3(main_7_out_3), .out_4(main_7_out_4),
    .out_5(main_7_out_5));  // open: out_6, out_7, out_8
  _7_Segment_Display u_7_segment_display_4 (
    .g(main_7_out_5), .f(main_7_out_4), .a(main_7_out_3), .b(main_7_out_2), .e(main_8_out_8),
    .d(main_8_out_7), .c(main_8_out_6));  // open: dp
  _7_segment_driver_main main_8 (
    .in_1(RES_OUT[11:8]), .out_6(main_8_out_6), .out_7(main_8_out_7), .out_8(main_8_out_8));  // open: out_2, out_3, out_4, out_5
  _16_bit_register u_16_bit_register_2 (.IN(CPU_DOUT), .LD(TIME_LD), .CLK(CLK), .OUT(TIME_OUT));
  _7_segment_driver_main main_9 (
    .in_1(TIME_OUT[7:4]), .out_2(main_9_out_2), .out_3(main_9_out_3), .out_4(main_9_out_4),
    .out_5(main_9_out_5));  // open: out_6, out_7, out_8
  _7_Segment_Display u_7_segment_display_5 (
    .g(main_9_out_5), .f(main_9_out_4), .a(main_9_out_3), .b(main_9_out_2), .e(main_10_out_8),
    .d(main_10_out_7), .c(main_10_out_6));  // open: dp
  _7_segment_driver_main main_10 (
    .in_1(TIME_OUT[7:4]), .out_6(main_10_out_6), .out_7(main_10_out_7), .out_8(main_10_out_8));  // open: out_2, out_3, out_4, out_5
  _7_segment_driver_main main_11 (
    .in_1(RES_OUT[7:4]), .out_2(main_11_out_2), .out_3(main_11_out_3), .out_4(main_11_out_4),
    .out_5(main_11_out_5));  // open: out_6, out_7, out_8
  _7_Segment_Display u_7_segment_display_6 (
    .g(main_11_out_5), .f(main_11_out_4), .a(main_11_out_3), .b(main_11_out_2), .e(main_12_out_8),
    .d(main_12_out_7), .c(main_12_out_6));  // open: dp
  _7_segment_driver_main main_12 (
    .in_1(RES_OUT[7:4]), .out_6(main_12_out_6), .out_7(main_12_out_7), .out_8(main_12_out_8));  // open: out_2, out_3, out_4, out_5
  _7_segment_driver_main main_13 (
    .in_1(TIME_OUT[3:0]), .out_2(main_13_out_2), .out_3(main_13_out_3), .out_4(main_13_out_4),
    .out_5(main_13_out_5));  // open: out_6, out_7, out_8
  _7_Segment_Display u_7_segment_display_7 (
    .g(main_13_out_5), .f(main_13_out_4), .a(main_13_out_3), .b(main_13_out_2), .e(main_14_out_8),
    .d(main_14_out_7), .c(main_14_out_6));  // open: dp
  _7_segment_driver_main main_14 (
    .in_1(TIME_OUT[3:0]), .out_6(main_14_out_6), .out_7(main_14_out_7), .out_8(main_14_out_8));  // open: out_2, out_3, out_4, out_5
  _7_segment_driver_main main_15 (
    .in_1(RES_OUT[3:0]), .out_2(main_15_out_2), .out_3(main_15_out_3), .out_4(main_15_out_4),
    .out_5(main_15_out_5));  // open: out_6, out_7, out_8
  _7_Segment_Display u_7_segment_display_8 (
    .g(main_15_out_5), .f(main_15_out_4), .a(main_15_out_3), .b(main_15_out_2), .e(main_16_out_8),
    .d(main_16_out_7), .c(main_16_out_6));  // open: dp
  _7_segment_driver_main main_16 (
    .in_1(RES_OUT[3:0]), .out_6(main_16_out_6), .out_7(main_16_out_7), .out_8(main_16_out_8));  // open: out_2, out_3, out_4, out_5

  // Other names for the same wires on the sheet: IN_SEL[1:0] = ADDR[1:0]; OUT_SEL = ADDR[0]; SW_1[15:0] = switch_1;
  //   SW_2[15:0] = switch_2
endmodule

module timer (
  input  CLK,
  output TIME_INT,
  output [15:0] TIME
);

  wire [10:0] counter_1_q;

  Counter #(.width(12), .max('hfff)) counter_1 (
    .count(CLK), .Q({TIME_INT, counter_1_q}), .clk(CLK), .clr(TIME_INT));  // open: load, D, carry
  Counter #(.width(16), .max('hffff)) counter_2 (
    .count(TIME_INT), .Q(TIME), .clk(TIME_INT));  // open: load, D, carry, clr
endmodule
